// Logisim project seven segmet display.circ as structural Verilog: 1 circuit, main circuit main
module main (
  input  in_1,
  output a,
  output b,
  output c,
  output d,
  output e,
  output f,
  output g
);

  wire and_1_out, clock_1_out, decoder_1_out0, decoder_1_out1, decoder_1_out2, decoder_1_out3,
       decoder_1_out4, decoder_1_out5, decoder_1_out6, decoder_1_out7, or_1_out, or_2_out, or_5_out,
       or_6_out, or_8_out, or_10_out, or_12_out, or_14_out;
  wire [2:0] j_k_ff_3_q;

  and and_1 (and_1_out, j_k_ff_3_q[0], j_k_ff_3_q[1]);
  J_K_Flip_Flop j_k_ff_1 (
    .J(and_1_out), .clk(clock_1_out), .K(and_1_out), .Q(j_k_ff_3_q[2]));  // open: Qn, preset, en, reset
  Clock clock_1 (.out(clock_1_out));
  J_K_Flip_Flop j_k_ff_2 (
    .J(j_k_ff_3_q[0]), .clk(clock_1_out), .K(j_k_ff_3_q[0]), .Q(j_k_ff_3_q[1]));  // open: Qn, preset, en, reset
  J_K_Flip_Flop j_k_ff_3 (.J(in_1), .clk(clock_1_out), .K(in_1), .Q(j_k_ff_3_q[0]));  // open: Qn, preset, en, reset
  Decoder #(.select(3)) decoder_1 (
    .out0(decoder_1_out0), .out1(decoder_1_out1), .out2(decoder_1_out2), .out3(decoder_1_out3),
    .out4(decoder_1_out4), .out5(decoder_1_out5), .out6(decoder_1_out6), .out7(decoder_1_out7),
    .sel(j_k_ff_3_q));  // open: en
  or or_1 (or_1_out, decoder_1_out3, decoder_1_out4, decoder_1_out7);
  or or_2 (or_2_out, decoder_1_out0, decoder_1_out1, decoder_1_out2);
  or or_3 (a, or_2_out, or_1_out);
  or or_4 (b, decoder_1_out3, decoder_1_out4, decoder_1_out5);
  or or_5 (or_5_out, decoder_1_out0, decoder_1_out1, decoder_1_out2);
  or or_6 (or_6_out, decoder_1_out1, decoder_1_out4, decoder_1_out5);
  or or_7 (c, or_6_out, decoder_1_out7);
  or or_8 (or_8_out, decoder_1_out3, decoder_1_out4, decoder_1_out7);
  or or_9 (d, or_5_out, or_8_out);
  or or_10 (or_10_out, decoder_1_out0, decoder_1_out1, decoder_1_out2);
  or or_11 (e, decoder_1_out0, decoder_1_out2, decoder_1_out3);
  or or_12 (or_12_out, decoder_1_out1, decoder_1_out2, decoder_1_out3);
  or or_13 (f, or_10_out, decoder_1_out7);
  or or_14 (or_14_out, decoder_1_out4, decoder_1_out6, decoder_1_out7);
  or or_15 (g, or_12_out, or_14_out);
  _7_Segment_Display u_7_segment_display_1 (.g(g), .f(f), .a(a), .b(b), .e(e), .d(d), .c(c));  // open: dp
endmodule
